# Fritzing sketch rangkaian esp32 suhu dan kelembapan (saved by Fritzing 0.8.7b)
breadboards: 1

parts:
  R1 = Resistor [tolerance=±5% resistance=220 package=THT]
  LED1 = LED - 5mm [color="Red (633nm)" package="5 mm [THT]"]
  U1 = ESP32-38PinWide [part_number=ESP32-38PinWide]
  DHT1 = DHT22 Humidity and Temperature Sensor

nets:
  GND: R1.Pin_0, U1.GND, DHT1.GND
  N1: R1.Pin_1, LED1.cathode
  N2: LED1.anode, U1.GPIO23
  N3: U1.3.3, DHT1.VDD
  N4: U1.GPIO4, DHT1.DATA

custom parts:
  ESP32-38PinWide: Generic 38-Pin ESP32 with wide format (only access to one side of pins on a breadboard) based on Stephen Lilley's HiLetgo ESP-WROOM-32 ESP32 ESP-32S Development Board.
